// Logisim project alu.circ as structural Verilog: 6 circuits, main circuit main
module main (
  input  [31:0] X,
  input  [31:0] Y,
  input  [5:0] Switch__S,
  output Signed_Overflow,
  output [31:0] RESULT,
  output Equal
);

  wire add, and_2_out, and_3_out, bitpal_1_out, comparator_3_lt, comparator_4_lt, o1, o2, sub;
  wire [4:0] bit_extender_1_out;
  wire [31:0] add_1_out, adder_1_out, and_1_out, bit_extender_2_out, bit_extender_3_out, bit_extender_4_out,
       lfsr_1_out, multiplexer_1_out, multiplexer_2_out, or_1_out, shifter_1_out, shifter_2_out,
       shifter_3_out, sub_1_out, subtractor_1_out;

  Comparator #(.width(6)) comparator_1 (.a(Switch__S), .b(6'b100000), .eq(add));  // open: gt, lt
  Comparator #(.width(6)) comparator_2 (.a(Switch__S), .b(6'b100001), .eq(sub));  // open: gt, lt
  Bit_Extender #(.in_width(32), .out_width(5)) bit_extender_1 (.in(Y), .out(bit_extender_1_out));
  Shifter #(.width(32)) shifter_1 (.in(X), .\dist (bit_extender_1_out), .out(shifter_1_out));
  Shifter #(.width(32), .shift("lr")) shifter_2 (.in(X), .\dist (bit_extender_1_out), .out(shifter_2_out));
  Shifter #(.width(32), .shift("ar")) shifter_3 (.in(X), .\dist (bit_extender_1_out), .out(shifter_3_out));
  add add_1 (.in_1(X), .in_2(Y), .out(add_1_out), .overflow(o1));
  Adder #(.width(32)) adder_1 (.a(X), .b(Y), .out(adder_1_out));  // open: cin, cout
  sub sub_1 (.in_1(X), .in_2(Y), .out(sub_1_out), .overflow(o2));
  Subtractor #(.width(32)) subtractor_1 (.a(X), .b(Y), .out(subtractor_1_out));  // open: bin, bout
  assign and_1_out = X & Y;  // AND_Gate and_1, 32 bits wide
  assign or_1_out = X | Y;  // OR_Gate or_1, 32 bits wide
  Comparator #(.width(32)) comparator_3 (.a(X), .b(Y), .eq(Equal), .lt(comparator_3_lt));  // open: gt
  Comparator #(.width(32), .mode("unsigned")) comparator_4 (.a(X), .b(Y), .lt(comparator_4_lt));  // open: gt, eq
  bitpal bitpal_1 (.in_1(X), .out(bitpal_1_out));
  lfsr lfsr_1 (.in_1(X), .out(lfsr_1_out));
  Multiplexer #(.select(2), .width(32)) multiplexer_1 (
    .in0(shifter_1_out), .in1(shifter_1_out), .in2(shifter_2_out), .in3(shifter_3_out),
    .out(multiplexer_1_out), .sel(Switch__S[1:0]));  // open: en
  assign bit_extender_2_out = {{31{1'b0}}, comparator_3_lt};  // Bit_Extender bit_extender_2
  assign bit_extender_3_out = {{31{1'b0}}, comparator_4_lt};  // Bit_Extender bit_extender_3
  assign bit_extender_4_out = {{31{1'b0}}, bitpal_1_out};  // Bit_Extender bit_extender_4
  Multiplexer #(.select(5), .width(32)) multiplexer_2 (
    .in0(add_1_out), .in1(adder_1_out), .in2(sub_1_out), .in3(subtractor_1_out), .in4(and_1_out),
    .in5(or_1_out), .in10(bit_extender_2_out), .in11(bit_extender_3_out), .in30(bit_extender_4_out),
    .in31(lfsr_1_out), .out(multiplexer_2_out), .sel(Switch__S[4:0]));  // open: in6, in7, in8, in9, in12, in13, in14, in15, in16, in17, in18, in19, in20, in21, in22, in23, in24, in25, in26, in27, in28, in29, en
  and and_2 (and_2_out, add, o1);
  and and_3 (and_3_out, sub, o2);
  or or_2 (Signed_Overflow, and_2_out, and_3_out);
  Multiplexer #(.width(32)) multiplexer_3 (
    .in0(multiplexer_1_out), .in1(multiplexer_2_out), .out(RESULT), .sel(Switch__S[5]));  // open: en

  // Other names for the same wires on the sheet: eq = Equal; select[4:0] = Switch__S[4:0]; s5 = Switch__S[5]

  // Notes on the sheet:
  //   INPUTS to your circuit
  //   INPUT to your circuit
  //   DON'T CHANGE THE INPUTS AND OUTPUTS! IF YOU DO SO, YOU NEED TO MAKE SURE THE PINS ARE IN THE RIGHT PLACES!
  //   OUTPUTS of your circuit
endmodule

module add (
  input  [31:0] in_1,
  input  [31:0] in_2,
  output [31:0] out,
  output overflow
);

  wire and_1_out, and_2_out;

  Adder #(.width(32)) adder_1 (.a(in_1), .b(in_2), .out(out));  // open: cin, cout
  and and_1 (and_1_out, ~in_1[31], ~in_2[31], out[31]);  // AND_Gate
  and and_2 (and_2_out, in_1[31], in_2[31], ~out[31]);  // AND_Gate
  or or_1 (overflow, and_1_out, and_2_out);
endmodule

module sub (
  input  [31:0] in_1,
  input  [31:0] in_2,
  output [31:0] out,
  output overflow
);

  wire and_1_out, and_2_out;

  Subtractor #(.width(32)) subtractor_1 (.a(in_1), .b(in_2), .out(out));  // open: bin, bout
  and and_1 (and_1_out, ~in_1[31], in_2[31], out[31]);  // AND_Gate
  and and_2 (and_2_out, in_1[31], ~in_2[31], ~out[31]);  // AND_Gate
  or or_1 (overflow, and_1_out, and_2_out);
endmodule

module bitpal (
  input  [31:0] in_1,
  output out
);

  Comparator #(.width(16)) comparator_1 (
    .a(in_1[15:0]),
    .b({in_1[16], in_1[17], in_1[18], in_1[19], in_1[20], in_1[21], in_1[22], in_1[23], in_1[24], in_1[25], in_1[26], in_1[27], in_1[28], in_1[29], in_1[30], in_1[31]}),
    .eq(out));  // open: gt, lt
endmodule

module lfsr (
  input  [31:0] in_1,
  output [31:0] out
);

  wire [0:0] xor_1_out;

  ExactlyOne xor_1 (.out(xor_1_out[0]), .in0(in_1[0]), .in1(in_1[2]), .in2(in_1[3]), .in3(in_1[5]));
  Shifter #(.width(32), .shift("rr")) shifter_1 (.in({in_1[31:1], xor_1_out[0]}), .\dist (5'b00001), .out(out));
  // Probe on out
endmodule

module my__mux (
  input  [31:0] in_1,
  input  [31:0] in_2
);

  Multiplexer #(.select(5), .width(32)) multiplexer_1 ();  // open: in0, in1, in2, in3, in4, in5, in6, in7, in8, in9, in10, in11, in12, in13, in14, in15, in16, in17, in18, in19, in20, in21, in22, in23, in24, in25, in26, in27, in28, in29, in30, in31, out, sel, en
  Multiplexer #(.select(5), .width(32)) multiplexer_2 ();  // open: in0, in1, in2, in3, in4, in5, in6, in7, in8, in9, in10, in11, in12, in13, in14, in15, in16, in17, in18, in19, in20, in21, in22, in23, in24, in25, in26, in27, in28, in29, in30, in31, out, sel, en
  Multiplexer #(.width(32)) multiplexer_3 ();  // open: in0, in1, out, sel, en
endmodule
