// Logisim project cpu.circ as structural Verilog: 4 circuits, main circuit main
module main (
  input  [31:0] RS_READ_VALUE,
  input  [31:0] RT_READ_VALUE,
  input  [31:0] INSTRUCTION,
  input  CLOCK,
  input  RESET,
  output [31:0] t0,
  output [31:0] t1,
  output [31:0] t2,
  output [31:0] t3,
  output [4:0] RS,
  output [4:0] RT,
  output [4:0] Write_Register,
  output [31:0] RD_WRITE_VALUE,
  output RD_WRITE_ENABLE,
  output [23:0] FETCH_ADDRESS
);

  wire ALU_equal, ALU_signed_overflow, ALUsrc, and_2_out, and_3_out, and_4_out, beq, bne, byteRd, J, jal, jr,
       lui, memToReg, mWr, nop, or_1_out, rf1_1_regf1, rf1_2_regf1, rf1_3_regf1, rf1_4_regf1, rWr, shiftInst,
       signExt;
  wire [1:0] wrSrc;
  wire [4:0] rd, shamt;
  wire [5:0] ALUop, funct, op;
  wire [15:0] immd;
  wire [23:0] adder_1_out, adder_2_out, bit_extender_4_out, bit_extender_5_out, bit_extender_6_out,
       multiplexer_9_out, multiplexer_10_out, nextPC, subtractor_1_out;
  wire [25:0] label;
  wire [31:0] ALU_result, bit_extender_1_out, bit_extender_2_out, bit_extender_3_out, bit_extender_7_out,
       MEM_data_mem_out, multiplexer_1_out, multiplexer_3_out, multiplexer_4_out, multiplexer_5_out,
       multiplexer_7_out, multiplexer_8_out, multiplexer_12_out, multiplexer_13_out, rsReadVal, rsReadVal2,
       rtReadVal2, shifter_1_out, shifter_2_out;

  RF1 rf1_1 (.in_1(Write_Register), .regF1(rf1_1_regf1));
  Register #(.width(24)) PC (.D(nextPC), .Q(FETCH_ADDRESS), .clk(CLOCK));  // open: en, clr
  and and_1 (RD_WRITE_ENABLE, rWr, ~rf1_1_regf1);  // AND_Gate
  Control control_1 (
    .funct(funct), .opcode(op), .jr(jr), .bne(bne), .beq(beq), .wrSrc(wrSrc), .rWr(rWr), .jal(jal),
    .ALUsrc(ALUsrc), .shiftInst(shiftInst), .signExt(signExt), .ALUop(ALUop), .byteRd(byteRd), .mWr(mWr),
    .memToReg(memToReg), .lui(lui), .J(J));
  Multiplexer #(.width(32)) multiplexer_1 (
    .in0(INSTRUCTION), .in1({32{1'b0}}), .out(multiplexer_1_out), .sel(nop));  // open: en
  PipelineReg PipelineReg (
    .in_1(multiplexer_1_out), .clk(CLOCK), .funct(funct), .shamt(shamt), .rd(rd), .rt(RT), .rs(RS),
    .opcode(op), .immediate(immd), .Label(label));
  Multiplexer #(.select(2), .width(5)) multiplexer_2 (
    .in0(RT), .in1(rd), .in2({5{1'b1}}), .in3({5{1'b1}}), .out(Write_Register), .sel(wrSrc));  // open: en
  assign bit_extender_1_out = {{16{1'b0}}, immd};  // Bit_Extender bit_extender_1
  assign bit_extender_2_out = {{16{immd[15]}}, immd};  // Bit_Extender bit_extender_2
  assign bit_extender_3_out = {{27{1'b0}}, shamt};  // Bit_Extender bit_extender_3
  regfile_main RegFile (
    .Read_register_1(RS[1:0]), .Read_register_2(RT[1:0]), .write_register(Write_Register[1:0]),
    .write_data(RD_WRITE_VALUE), .t0_Value(t0), .t1_Value(t1), .t2_Value(t2), .t3_Value(t3),
    .RegWrite(and_2_out), .clock(CLOCK), .Read_Data_1(rsReadVal2), .Read_Data_2(rtReadVal2));
  and and_2 (and_2_out, rWr, rf1_2_regf1);
  RF1 rf1_2 (.in_1(Write_Register), .regF1(rf1_2_regf1));
  Multiplexer #(.width(32)) multiplexer_3 (
    .in0(bit_extender_1_out), .in1(bit_extender_2_out), .out(multiplexer_3_out), .sel(signExt));  // open: en
  RF1 rf1_3 (.in_1(RS), .regF1(rf1_3_regf1));
  RF1 rf1_4 (.in_1(RT), .regF1(rf1_4_regf1));
  Multiplexer #(.width(32)) multiplexer_4 (
    .in0(RS_READ_VALUE), .in1(rsReadVal2), .out(multiplexer_4_out), .sel(rf1_3_regf1));  // open: en
  Multiplexer #(.width(32)) multiplexer_5 (
    .in0(RT_READ_VALUE), .in1(rtReadVal2), .out(multiplexer_5_out), .sel(rf1_4_regf1));  // open: en
  Bit_Extender #(.in_width(32), .out_width(24), .\type ("sign")) bit_extender_4 (
    .in(multiplexer_3_out), .out(bit_extender_4_out));
  Shifter #(.width(32), .shift("ar")) shifter_1 (.in(rsReadVal), .\dist (5'b00010), .out(shifter_1_out));
  Bit_Extender #(.in_width(26), .out_width(24)) bit_extender_5 (.in(label), .out(bit_extender_5_out));
  Multiplexer #(.width(32)) multiplexer_6 (
    .in0(multiplexer_4_out), .in1(multiplexer_5_out), .out(rsReadVal), .sel(shiftInst));  // open: en
  Multiplexer #(.width(32)) multiplexer_7 (
    .in0(multiplexer_5_out), .in1(multiplexer_3_out), .out(multiplexer_7_out), .sel(ALUsrc));  // open: en
  Adder #(.width(24)) adder_1 (.a(FETCH_ADDRESS), .b(24'h1), .out(adder_1_out));  // open: cin, cout
  Adder #(.width(24)) adder_2 (.a(FETCH_ADDRESS), .b(bit_extender_4_out), .out(adder_2_out));  // open: cin, cout
  Bit_Extender #(.in_width(32), .out_width(24), .\type ("sign")) bit_extender_6 (
    .in(shifter_1_out), .out(bit_extender_6_out));
  Subtractor #(.width(24)) subtractor_1 (
    .a(bit_extender_5_out), .b(24'h100000), .out(subtractor_1_out));  // open: bin, bout
  Multiplexer #(.width(32)) multiplexer_8 (
    .in0(multiplexer_7_out), .in1(bit_extender_3_out), .out(multiplexer_8_out), .sel(shiftInst));  // open: en
  Multiplexer #(.width(24)) multiplexer_9 (
    .in0(adder_1_out), .in1(adder_2_out), .out(multiplexer_9_out), .sel(or_1_out));  // open: en
  LED led_1 (.in(ALU_signed_overflow));
  alu_main ALU (
    .Switch__S(ALUop), .X(rsReadVal), .Equal(ALU_equal), .RESULT(ALU_result),
    .Signed_Overflow(ALU_signed_overflow), .Y(multiplexer_8_out));
  and and_3 (and_3_out, beq, ALU_equal);
  or or_1 (or_1_out, and_3_out, and_4_out);
  Multiplexer #(.width(24)) multiplexer_10 (
    .in0(multiplexer_9_out), .in1(bit_extender_6_out), .out(multiplexer_10_out), .sel(jr));  // open: en
  Multiplexer #(.width(24)) multiplexer_11 (
    .in0(multiplexer_10_out), .in1(subtractor_1_out), .out(nextPC), .sel(J));  // open: en
  and and_4 (and_4_out, bne, ~ALU_equal);  // AND_Gate
  or or_2 (nop, or_1_out, jr, J);
  mem_main MEM (
    .Data_Mem_Addr(ALU_result), .Data_Mem_In(multiplexer_5_out), .ACCESS_BYTE(byteRd), .MEM_WRITE(mWr),
    .CLOCK(CLOCK), .Data_Mem_Out(MEM_data_mem_out));
  Multiplexer #(.width(32)) multiplexer_12 (
    .in0(ALU_result), .in1(MEM_data_mem_out), .out(multiplexer_12_out), .sel(memToReg));  // open: en
  Shifter #(.width(32)) shifter_2 (.in(multiplexer_3_out), .\dist (5'b10000), .out(shifter_2_out));
  Multiplexer #(.width(32)) multiplexer_13 (
    .in0(multiplexer_12_out), .in1(shifter_2_out), .out(multiplexer_13_out), .sel(lui));  // open: en
  Multiplexer #(.width(32)) multiplexer_14 (
    .in0(multiplexer_13_out), .in1(bit_extender_7_out), .out(RD_WRITE_VALUE), .sel(jal));  // open: en
  assign bit_extender_7_out = {{8{1'b0}}, FETCH_ADDRESS};  // Bit_Extender bit_extender_7

  // Other names for the same wires on the sheet: clk = CLOCK; data[31:0] = RD_WRITE_VALUE; PC[23:0] = FETCH_ADDRESS;
  //   rsReadVal1[31:0] = RS_READ_VALUE; rtReadVal1[31:0] = RT_READ_VALUE; wrReg[4:0] = Write_Register

  // Notes on the sheet:
  //   These are outputs/inputs from run.circ
  //   These are outputs to run.circ
  //   READ/DECODE
  //   EXECUTION 
  //   NEXT PC CALCULATION
  //   MEMORY R/W
endmodule

// Con trol
module Control (
  input  [5:0] opcode,
  input  [5:0] funct,
  output ALUsrc,
  output shiftInst,
  output signExt,
  output [5:0] ALUop,
  output byteRd,
  output mWr,
  output memToReg,
  output lui,
  output jr,
  output bne,
  output beq,
  output [1:0] wrSrc,
  output rWr,
  output jal,
  output J
);

  wire and_7_out, and_8_out, and_10_out, comparator_1_eq, comparator_2_eq, comparator_3_eq, comparator_5_eq,
       comparator_6_eq, comparator_7_eq, comparator_8_eq, comparator_9_eq, comparator_10_eq,
       comparator_11_eq, comparator_12_eq, comparator_13_eq, comparator_14_eq, comparator_15_eq,
       comparator_16_eq, comparator_17_eq, I, not_1_out, not_2_out, or_1_out, or_3_out, or_4_out, or_5_out,
       or_7_out, R;
  wire [1:0] multiplexer_1_out;

  not not_1 (not_1_out, R);
  not not_2 (not_2_out, J);
  Comparator #(.width(6)) comparator_1 (.a(funct), .b({6{1'b0}}), .eq(comparator_1_eq));  // open: gt, lt
  or or_1 (or_1_out, comparator_1_eq, comparator_2_eq, comparator_3_eq);
  Comparator #(.width(6)) comparator_2 (.a(funct), .b(6'b000011), .eq(comparator_2_eq));  // open: gt, lt
  Comparator #(.width(6)) comparator_3 (.a(funct), .b(6'b000011), .eq(comparator_3_eq));  // open: gt, lt
  Comparator #(.width(6)) comparator_4 (.a(opcode), .b({6{1'b0}}), .eq(R));  // open: gt, lt
  Comparator #(.width(6)) comparator_5 (.a(opcode), .b(6'b000011), .eq(comparator_5_eq));  // open: gt, lt
  Comparator #(.width(6)) comparator_6 (.a(opcode), .b(6'b000010), .eq(comparator_6_eq));  // open: gt, lt
  and and_1 (I, not_1_out, not_2_out);
  and and_2 (shiftInst, R, or_1_out);
  or or_2 (J, comparator_5_eq, comparator_6_eq);
  or or_3 (or_3_out, beq, bne);
  Comparator #(.width(6)) comparator_7 (.a(funct), .b(6'b001000), .eq(comparator_7_eq));  // open: gt, lt
  and and_3 (ALUsrc, I, ~or_3_out);  // AND_Gate
  and and_4 (jr, comparator_7_eq, R);
  Comparator #(.width(6)) comparator_8 (.a(opcode), .b(6'b001100), .eq(comparator_8_eq));  // open: gt, lt
  Comparator #(.width(6)) comparator_9 (.a(opcode), .b(6'b001101), .eq(comparator_9_eq));  // open: gt, lt
  Comparator #(.width(6)) comparator_10 (.a(6'b000101), .b(opcode), .eq(comparator_10_eq));  // open: gt, lt
  and and_5 (bne, I, comparator_10_eq);
  or or_4 (or_4_out, comparator_8_eq, comparator_9_eq);
  Comparator #(.width(6)) comparator_11 (.a(opcode), .b(6'b001111), .eq(comparator_11_eq));  // open: gt, lt
  Comparator #(.width(6)) comparator_12 (.a(6'b000100), .b(opcode), .eq(comparator_12_eq));  // open: gt, lt
  and and_6 (beq, comparator_12_eq, I);
  Comparator #(.width(6)) comparator_13 (.a(opcode), .b(6'b100100), .eq(comparator_13_eq));  // open: gt, lt
  Comparator #(.width(6)) comparator_14 (.a(opcode), .b(6'b100000), .eq(comparator_14_eq));  // open: gt, lt
  Multiplexer #(.width(2)) multiplexer_1 (.in0(2'b00), .in1(2'b01), .out(multiplexer_1_out), .sel(R));  // open: en
  Multiplexer #(.width(2)) multiplexer_2 (.in0(multiplexer_1_out), .in1(2'b10), .out(wrSrc), .sel(J));  // open: en
  or or_5 (or_5_out, comparator_13_eq, comparator_14_eq);
  and and_7 (and_7_out, ~jr, R);  // AND_Gate
  Comparator #(.width(6)) comparator_15 (.a(opcode), .b(6'b101011), .eq(comparator_15_eq));  // open: gt, lt
  Comparator #(.width(6)) comparator_16 (.a(opcode), .b(6'b100011), .eq(comparator_16_eq));  // open: gt, lt
  and and_8 (and_8_out, ALUsrc, I, ~mWr);  // AND_Gate
  or or_6 (rWr, and_7_out, and_8_out, and_10_out);
  and and_9 (byteRd, or_5_out, I);
  Comparator #(.width(6)) comparator_17 (.a(opcode), .b(6'b000011), .eq(comparator_17_eq));  // open: gt, lt
  and and_10 (and_10_out, J, jal);
  or or_7 (or_7_out, byteRd, comparator_16_eq);
  and and_11 (jal, comparator_17_eq, J);
  and and_12 (signExt, I, ~or_4_out);  // AND_Gate
  Multiplexer #(.width(6)) multiplexer_3 (.in0(funct), .in1(6'b100000), .out(ALUop), .sel(I));  // open: en
  and and_13 (mWr, I, comparator_15_eq);
  and and_14 (memToReg, I, or_7_out);
  and and_15 (lui, I, comparator_11_eq);
endmodule

module RF1 (
  input  [4:0] in_1,
  output regF1
);

  and and_1 (regF1, ~in_1[2], in_1[3], ~in_1[4]);  // AND_Gate
endmodule

module PipelineReg (
  input  [31:0] in_1,
  input  clk,
  output [5:0] funct,
  output [4:0] shamt,
  output [4:0] rd,
  output [4:0] rt,
  output [4:0] rs,
  output [5:0] opcode,
  output [15:0] immediate,
  output [25:0] Label
);

  Register #(.width(32)) register_1 (
    .D(in_1), .Q({opcode, Label[25:16], immediate[15:6], funct}), .clk(clk));  // open: en, clr

  assign immediate[5:0] = funct;
  assign Label[15:0] = {immediate[15:6], funct};
  assign rd = immediate[15:11];
  assign rs = Label[25:21];
  assign rt = Label[20:16];
  assign shamt = immediate[10:6];
endmodule
