// Logisim project regfile.circ as structural Verilog: 1 circuit, main circuit main
module main (
  input  [1:0] Read_register_1,
  input  [1:0] Read_register_2,
  input  [1:0] write_register,
  input  [31:0] write_data,
  input  RegWrite,
  input  clock,
  output [31:0] t0_Value,
  output [31:0] t1_Value,
  output [31:0] t2_Value,
  output [31:0] t3_Value,
  output [31:0] Read_Data_1,
  output [31:0] Read_Data_2
);

  wire en0, en1, en2, en3;
  wire [31:0] demultiplexer_1_out0, demultiplexer_1_out1, demultiplexer_1_out2, demultiplexer_1_out3;

  Demultiplexer #(.select(2), .width(32)) demultiplexer_1 (
    .out0(demultiplexer_1_out0), .out1(demultiplexer_1_out1), .out2(demultiplexer_1_out2),
    .out3(demultiplexer_1_out3), .in(write_data), .sel(write_register));  // open: en
  Demultiplexer #(.select(2)) demultiplexer_2 (
    .out0(en0), .out1(en1), .out2(en2), .out3(en3), .in(RegWrite), .sel(write_register));  // open: en
  Register #(.width(32)) t0 (.D(demultiplexer_1_out0), .en(en0), .Q(t0_Value), .clk(clock));  // open: clr
  Register #(.width(32)) t1 (.D(demultiplexer_1_out1), .en(en1), .Q(t1_Value), .clk(clock));  // open: clr
  Register #(.width(32)) t2 (.D(demultiplexer_1_out2), .en(en2), .Q(t2_Value), .clk(clock));  // open: clr
  Register #(.width(32)) t3 (.D(demultiplexer_1_out3), .en(en3), .Q(t3_Value), .clk(clock));  // open: clr
  Multiplexer #(.select(2), .width(32)) multiplexer_1 (
    .in0(t0_Value), .in1(t1_Value), .in2(t2_Value), .in3(t3_Value), .out(Read_Data_1), .sel(Read_register_1));  // open: en
  Multiplexer #(.select(2), .width(32)) multiplexer_2 (
    .in0(t0_Value), .in1(t1_Value), .in2(t2_Value), .in3(t3_Value), .out(Read_Data_2), .sel(Read_register_2));  // open: en

  // Other names for the same wires on the sheet: rReg1[1:0] = Read_register_1; rReg2[1:0] = Read_register_2;
  //   t0val[31:0] = t0_Value; t1val[31:0] = t1_Value; t2val[31:0] = t2_Value; t3val[31:0] = t3_Value;
  //   WriteReg[1:0] = write_register

  // Notes on the sheet:
  //   These are INPUTS to the circuit
  //   These are INPUTS to the circuit
  //   DO NOT CHANGE THE LOCATIONS OF THE INPUTS/OUTPUTS! IF YOU DO SO, YOU NEED TO MAKE SURE THE PINS ARE AT THE RIGHT PLACE!
  //   These are OUTPUTS to the circuit
  //   Yet again, the clock is not an actual clock, but an input, one that will be driven from a higher circuit
  //   These are OUTPUTS to the circuit
endmodule
